// Logisim project cpu.circ as structural Verilog: 1 circuit, main circuit cpu
module cpu (
  input  clk,
  input  [31:0] Instruction,
  input  [31:0] MemReadData,
  output [31:0] MemAddress,
  output [31:0] ProgramCounter,
  output [31:0] ra,
  output [31:0] sp,
  output [31:0] t0,
  output [31:0] t1,
  output [31:0] t2,
  output [31:0] s0,
  output [31:0] s1,
  output [31:0] a0,
  output [3:0] MemWriteMask,
  output [31:0] MemWriteData
);

  wire ASel, BrEq, BrLt, BrUn, BSel, MemWen, PCSel, RegWEn;
  wire [1:0] WBSel;
  wire [2:0] ImmSel;
  wire [3:0] ALUSel;
  wire [31:0] imm_gen_1_immediate, multiplexer_1_out, multiplexer_2_out, multiplexer_3_out,
       partial_load_1_datatoreg, PC_add_4, regfile_1_readdata1, RegWriteData, rs2;

  Adder #(.width(32)) adder_1 (.a(ProgramCounter), .b(32'h4), .out(PC_add_4));  // open: cin, cout
  Multiplexer #(.width(32)) multiplexer_1 (.in0(PC_add_4), .in1(MemAddress), .out(multiplexer_1_out), .sel(PCSel));
  Register #(.width(32)) PC (.D(multiplexer_1_out), .clk(clk), .Q(ProgramCounter));  // open: en, clr
  control_logic control_logic_1 (
    .Instruction(Instruction), .BrEq(BrEq), .BrLt(BrLt), .PCSel(PCSel), .RegWEn(RegWEn), .ImmSel(ImmSel),
    .BrUn(BrUn), .ASel(ASel), .BSel(BSel), .ALUSel(ALUSel), .MemWEn(MemWen), .WBSel(WBSel));
  regfile regfile_1 (
    .ReadIndex1(Instruction[19:15]), .ReadIndex2(Instruction[24:20]), .WriteIndex(Instruction[11:7]),
    .WriteData(RegWriteData), .RegWEn(RegWEn), .clk(clk), .ra(ra), .sp(sp), .t0(t0), .t1(t1), .t2(t2),
    .s0(s0), .s1(s1), .a0(a0), .ReadData1(regfile_1_readdata1), .ReadData2(rs2));
  imm_gen imm_gen_1 (.Instruction(Instruction), .ImmSel(ImmSel), .Immediate(imm_gen_1_immediate));
  Multiplexer #(.width(32)) multiplexer_2 (
    .in0(regfile_1_readdata1), .in1(ProgramCounter), .out(multiplexer_2_out), .sel(ASel));
  Multiplexer #(.width(32)) multiplexer_3 (.in0(rs2), .in1(imm_gen_1_immediate), .out(multiplexer_3_out), .sel(BSel));
  alu alu_1 (.A(multiplexer_2_out), .B(multiplexer_3_out), .ALUSel(ALUSel), .ALUResult(MemAddress));
  branch_comp branch_comp_1 (.BrData1(regfile_1_readdata1), .BrData2(rs2), .BrUn(BrUn), .BrEq(BrEq), .BrLt(BrLt));
  partial_store partial_store_1 (
    .Instruction(Instruction), .MemAddress(MemAddress), .DataFromReg(rs2), .MemWEn(MemWen),
    .MemWriteMask(MemWriteMask), .DataToMem(MemWriteData));
  partial_load partial_load_1 (
    .Instruction(Instruction), .MemAddress(MemAddress), .DataFromMem(MemReadData),
    .DataToReg(partial_load_1_datatoreg));
  Multiplexer #(.select(2), .width(32)) multiplexer_4 (
    .in0(partial_load_1_datatoreg), .in1(MemAddress), .in2(PC_add_4), .out(RegWriteData), .sel(WBSel));  // open: in3

  // Notes on the sheet:
  //   To IMEM
  //   IMEM (do **NOT** move this)
  //   From IMEM
  //   Inputs/Outputs for testing. Do **NOT** move these.
  //   To DMEM
  //   DMEM (do **NOT** move this)
  //   From DMEM
endmodule
